# Fritzing sketch Prototyp_1 (saved by Fritzing 0.9.3b)

parts:
  MH-ET_LIVE_ESP32_DEVKIT1 = MH-ET LIVE ESP32 DEVKIT 38 pins
  Bauteil1 = BME280
  RFM95W1 = RFM95W LoRa Module
  ANT1 = Antenna

nets:
  N1: MH-ET_LIVE_ESP32_DEVKIT1.3V3, RFM95W1.12_DIO4, RFM95W1.13_3.3V
  N2: MH-ET_LIVE_ESP32_DEVKIT1.IO14, RFM95W1.6_RESET, RFM95W1.7_DIO5
  N3: MH-ET_LIVE_ESP32_DEVKIT1.GND#58, Bauteil1.GND
  5V: MH-ET_LIVE_ESP32_DEVKIT1.5V, Bauteil1.VIN
  N4: MH-ET_LIVE_ESP32_DEVKIT1.GND#64, RFM95W1.1_GND, RFM95W1.8_GND
  N5: MH-ET_LIVE_ESP32_DEVKIT1.IO23, RFM95W1.3_MOSI
  N6: MH-ET_LIVE_ESP32_DEVKIT1.IO22, Bauteil1.SCL
  N7: MH-ET_LIVE_ESP32_DEVKIT1.IO21, Bauteil1.SDA
  N8: MH-ET_LIVE_ESP32_DEVKIT1.IO19, RFM95W1.2_MISO
  N9: MH-ET_LIVE_ESP32_DEVKIT1.IO18, RFM95W1.4_SCK
  N10: MH-ET_LIVE_ESP32_DEVKIT1.IO5, RFM95W1.5_NSS_(CS)
  N11: MH-ET_LIVE_ESP32_DEVKIT1.IO2, RFM95W1.14_DIO0
  N12: MH-ET_LIVE_ESP32_DEVKIT1.IO15, RFM95W1.15_DIO1
  N13: RFM95W1.9_ANT, ANT1.antenna_lead

notes:
  Protoyp 1
  ESP32 + RFM95 + BME280

custom parts:
  MH-ET LIVE ESP32 DEVKIT 38 pins: http://mh.nodebb.com/topic/2/mh-et-live-esp32-devkit
  RFM95W LoRa Module: RF Transceiver by Hope RF. Well supported Arduino libraries are available. This Low Power Long Range Transceiver Module for the frequencies 868MHz and 915MHz and it is also available in other versions.
